// Logisim project LOGIKAGRY (1).circ as structural Verilog: 1 circuit, main circuit main
// stan_pion
module main (
  input  sygnal_losowania,
  input  [10:0] pion_info_odczyt,
  input  [1:0] IN_ruch_ktorym_pionem,
  input  [1:0] IN_ktory_gracz,
  output CLK_SAVE,
  output [10:0] out_6,
  output [10:0] out_7,
  output [3:0] out_8,
  output ZAPISZZ,
  output out_10,
  output [6:0] out_11,
  output [10:0] Pion_Dane_do_zapisu
);

  wire and_2_out, and_3_out, and_4_out, and_5_out, and_6_out, and_7_out, and_8_out, and_9_out, and_10_out,
       and_11_out, and_12_out, and_13_out, bool_ruch_zapis, clock_1_out, clock_2_out, clock_3_out,
       comparator_1_eq, comparator_2_eq, comparator_3_eq, comparator_3_lt, comparator_8_gt, comparator_10_eq,
       comparator_10_gt, comparator_10_lt, comparator_11_eq, comparator_12_eq, comparator_13_gt,
       comparator_14_eq, comparator_15_eq, info, multiplexer_1_out, nand_1_out, nand_2_out, nand_3_out,
       nand_4_out, nand_6_out, nie_wyjscie, not_1_out, not_2_out, not_3_out, not_4_out, not_5_out, not_6_out,
       not_7_out, not_8_out, or_1_out, or_4_out, or_5_out, pionek_ruch, pionek_zezwolenie, player_blue,
       player_green, player_red, player_yellow, wykryta_kolizja;
  wire [1:0] counter_1_q;
  wire [3:0] rzut_liczba;
  wire [6:0] adder_1_out, adder_2_out, multiplexer_3_out, multiplexer_4_out, subtractor_2_out,
       transistor_6_out;

  random_generaor_main main_1 (.Cyfra(rzut_liczba), .out_2(info), .Kropka(out_10), .Losuj(sygnal_losowania));
  Comparator #(.width(2), .mode("unsigned")) comparator_1 (
    .a(pion_info_odczyt[8:7]), .b(IN_ruch_ktorym_pionem), .eq(comparator_1_eq));  // open: gt, lt
  Comparator #(.width(2), .mode("unsigned")) comparator_2 (
    .a(pion_info_odczyt[10:9]), .b(IN_ktory_gracz), .eq(comparator_2_eq));  // open: gt, lt
  Hex_Digit_Display hex_digit_display_1 (.value(rzut_liczba));  // open: dp
  and and_1 (pionek_zezwolenie, comparator_1_eq, comparator_2_eq);
  Comparator #(.width(7)) comparator_3 (
    .a(pion_info_odczyt[6:0]), .b(7'b0001111), .gt(pionek_ruch), .eq(comparator_3_eq), .lt(comparator_3_lt));
  Comparator #(.width(2), .mode("unsigned")) comparator_4 (
    .a(pion_info_odczyt[10:9]), .b(2'b00), .eq(player_red));  // open: gt, lt
  Comparator #(.width(2), .mode("unsigned")) comparator_5 (
    .a(pion_info_odczyt[10:9]), .b(2'b01), .eq(player_blue));  // open: gt, lt
  Comparator #(.width(2), .mode("unsigned")) comparator_6 (
    .a(pion_info_odczyt[10:9]), .b(2'b10), .eq(player_green));  // open: gt, lt
  Comparator #(.width(2), .mode("unsigned")) comparator_7 (
    .a(pion_info_odczyt[10:9]), .b(2'b11), .eq(player_yellow));  // open: gt, lt
  Register #(.width(4)) register_1 (.D(rzut_liczba), .Q(out_8), .clk(multiplexer_1_out));  // open: en, clr
  Multiplexer #(.enable("false")) multiplexer_1 (.in0(1'b0), .in1(clock_1_out), .out(multiplexer_1_out), .sel(info));
  Clock clock_1 (.out(clock_1_out));
  or or_1 (or_1_out, comparator_3_eq, comparator_3_lt);
  nand nand_1 (nand_1_out, out_10, or_1_out, player_red, pionek_zezwolenie);
  nand nand_2 (nand_2_out, out_10, or_1_out, player_blue, pionek_zezwolenie);
  nand nand_3 (nand_3_out, out_10, or_1_out, player_green, pionek_zezwolenie);
  nand nand_4 (nand_4_out, out_10, or_1_out, player_yellow, pionek_zezwolenie);
  and and_2 (and_2_out, out_10, pionek_zezwolenie, info);
  and and_3 (and_3_out, info, bool_ruch_zapis, pionek_ruch, pionek_zezwolenie);
  not not_1 (not_1_out, out_10);
  Transistor #(.width(7)) transistor_1 (.in(7'b0010000), .out(Pion_Dane_do_zapisu[6:0]), .gate(nand_1_out));
  Transistor #(.width(7)) transistor_2 (.in(7'b0011010), .out(Pion_Dane_do_zapisu[6:0]), .gate(nand_2_out));
  Transistor #(.width(7)) transistor_3 (.in(7'b0100100), .out(Pion_Dane_do_zapisu[6:0]), .gate(nand_3_out));
  or or_2 (ZAPISZZ, and_2_out, and_3_out, wykryta_kolizja);
  nand nand_5 (nie_wyjscie, info, not_1_out, or_1_out);
  Transistor #(.width(7)) transistor_4 (.in(7'b0101110), .out(Pion_Dane_do_zapisu[6:0]), .gate(nand_4_out));
  not not_2 (not_2_out, ZAPISZZ);
  Clock clock_2 (.out(clock_2_out));
  Transistor #(.width(7)) transistor_5 (.in(pion_info_odczyt[6:0]), .out(Pion_Dane_do_zapisu[6:0]), .gate(nie_wyjscie));
  Multiplexer #(.enable("false")) multiplexer_2 (.in0(clock_2_out), .in1(1'b0), .out(CLK_SAVE), .sel(not_2_out));
  and and_4 (and_4_out, info, pionek_ruch, player_red);
  and and_5 (and_5_out, info, pionek_ruch, player_blue);
  and and_6 (and_6_out, info, pionek_ruch, player_green);
  and and_7 (and_7_out, info, pionek_ruch, player_yellow);
  and and_8 (and_8_out, ZAPISZZ, not_4_out);
  not not_3 (not_3_out, pionek_ruch);
  or or_3 (bool_ruch_zapis, and_4_out, or_4_out);
  Register #(.width(11), .trigger("falling")) register_2 (
    .D({pion_info_odczyt[10:7], Pion_Dane_do_zapisu[6:0]}), .Q(out_7), .clk(and_8_out), .clr(comparator_12_eq));  // open: en
  not not_4 (not_4_out, wykryta_kolizja);
  Transistor #(.width(7)) transistor_6 (.in({3'b000, rzut_liczba}), .out(transistor_6_out), .gate(not_3_out));
  Comparator #(.width(7), .mode("unsigned")) comparator_8 (
    .a(adder_1_out), .b(7'b0110111), .gt(comparator_8_gt));  // open: eq, lt
  Comparator #(.width(7), .mode("unsigned")) comparator_9 (.a(adder_1_out), .b(7'b0111011));  // open: gt, eq, lt
  or or_4 (or_4_out, and_5_out, and_6_out, and_7_out);
  Clock clock_3 (.out(clock_3_out));
  Adder #(.width(7)) adder_1 (.a(transistor_6_out), .b(pion_info_odczyt[6:0]), .out(adder_1_out));  // open: cin, cout
  and and_9 (and_9_out, comparator_8_gt, or_4_out);
  Comparator #(.width(2), .mode("unsigned")) comparator_10 (
    .a(pion_info_odczyt[10:9]), .b(out_7[10:9]), .gt(comparator_10_gt), .eq(comparator_10_eq),
    .lt(comparator_10_lt));
  Comparator #(.width(7), .mode("unsigned")) comparator_11 (
    .a(out_7[6:0]), .b(pion_info_odczyt[6:0]), .eq(comparator_11_eq));  // open: gt, lt
  and and_10 (and_10_out, wykryta_kolizja, clock_3_out);
  Multiplexer #(.width(7), .enable("false")) multiplexer_3 (
    .in0({7{1'b0}}), .in1(7'b0101000), .out(multiplexer_3_out), .sel(and_9_out));
  and and_11 (and_11_out, comparator_10_eq, comparator_11_eq);
  or or_5 (or_5_out, comparator_10_gt, comparator_10_lt);
  and and_12 (and_12_out, or_5_out, comparator_11_eq);
  Counter #(.width(2), .max('h3)) counter_1 (
    .Q(counter_1_q), .clk(and_10_out), .clr(comparator_12_eq));  // open: load, D, count, carry
  Subtractor #(.width(7)) subtractor_1 (
    .a(adder_1_out), .b(multiplexer_3_out), .out(Pion_Dane_do_zapisu[6:0]));  // open: bin, bout
  or or_6 (wykryta_kolizja, and_12_out, not_5_out);
  Comparator #(.width(2), .mode("unsigned")) comparator_12 (
    .a(counter_1_q), .b(2'b11), .eq(comparator_12_eq));  // open: gt, lt
  Comparator #(.width(7), .mode("unsigned")) comparator_13 (
    .a(pion_info_odczyt[6:0]), .b(7'b0001111), .gt(comparator_13_gt));  // open: eq, lt
  Comparator #(.width(7), .mode("unsigned")) comparator_14 (
    .a({7{1'b0}}), .b(pion_info_odczyt[6:0]), .eq(comparator_14_eq));  // open: gt, lt
  not not_5 (not_5_out, nand_6_out);
  not not_6 (not_6_out, comparator_14_eq);
  Multiplexer #(.select(2), .width(7), .enable("false")) multiplexer_4 (
    .in0({7{1'b0}}), .in1(7'b0000100), .in2(7'b0001000), .in3(7'b0001100), .out(multiplexer_4_out),
    .sel(pion_info_odczyt[10:9]));
  and and_13 (and_13_out, and_11_out, comparator_13_gt, not_6_out);
  not not_7 (not_7_out, and_12_out);
  Adder #(.width(7)) adder_2 (
    .a(multiplexer_4_out), .b({{5{1'b0}}, pion_info_odczyt[8:7]}), .out(adder_2_out));  // open: cin, cout
  Transistor #(.width(7)) transistor_7 (.in(adder_2_out), .out(Pion_Dane_do_zapisu[6:0]), .gate(not_7_out));
  Subtractor #(.width(7)) subtractor_2 (
    .a(pion_info_odczyt[6:0]), .b(7'b0000001), .out(subtractor_2_out));  // open: bin, bout
  not not_8 (not_8_out, comparator_15_eq);
  nand nand_6 (nand_6_out, and_13_out, not_8_out);
  Transistor #(.width(7)) transistor_8 (.in(subtractor_2_out), .out(Pion_Dane_do_zapisu[6:0]), .gate(nand_6_out));
  Comparator #(.width(2), .mode("unsigned")) comparator_15 (
    .a(pion_info_odczyt[8:7]), .b(out_7[8:7]), .eq(comparator_15_eq));  // open: gt, lt

  assign out_6 = pion_info_odczyt;
  assign out_11 = pion_info_odczyt[6:0];
  assign Pion_Dane_do_zapisu[10:7] = pion_info_odczyt[10:7];

  // Other names for the same wires on the sheet: nr_pionka[1:0] = pion_info_odczyt[8:7]; dot = out_10;
  //   gracz_nr2bit[1:0] = IN_ktory_gracz; Pozycja[6:0] = pion_info_odczyt[6:0]; nr_pionka_kol[1:0] = out_7[8:7];
  //   stan_pion[6:0] = Pion_Dane_do_zapisu[6:0]; kolor[1:0] = pion_info_odczyt[10:9]; zapisz = ZAPISZZ

  // Notes on the sheet:
  //   Czerwony
  //   Niebieskiego
  //   Zielony
  //   Zółty
  //   Warunek czy pion jest na polu startowym
  //   #1 Wyjscie z bazy
  //   Warunki logiczne
  //   Force'owanie przerzucenia na pole start
  //   #2 poruszanie się po planszy
  //   sterowanie logiczne
  //   sterowanie na planszy/HANDLE przegięcie (B,G,Y)
  //   RESET PION
  //   DORZUCIC WARUNEK ZE ODEJMIE JEZELI NIE JEST W BAZIE!!!!!!!!!
  //   Bugfix zapisu przy kolizji
  //   Delay resetu przy kolizji
  //   Dorzucamy zmienna w pionku ktora bedzie mowic czy przeszla juz przez punkt przegiecia
  //   #4 wejście do bazy
  //   Potem juz latwiej sterowac logika przy bazie
  //   KOLIZJA Z INNYM GRACZEM
  //   Po kolizji reset zmiennej "przegiecia"
  //   KOLIZJA Z WŁASNYM PIONKIEM
  //   poprawic bo tu blad gdzies
  //   Narazie zostawimy bugged czerwonego bo dupa
  //   #3 Handle exceptions
  //   #5 WIN
endmodule
