// Logisim project LOGIKAGRY.circ as structural Verilog: 1 circuit, main circuit main
// stan_pion
module main (
  input  sygnal_losowania,
  input  [10:0] pion_info_odczyt,
  input  [1:0] IN_ruch_ktorym_pionem,
  input  [1:0] IN_ktory_gracz,
  output [6:0] out_5,
  output zapisz_dane,
  output [10:0] Pion_Dane_do_zapisu
);

  wire and_1_out, and_2_out, and_3_out, and_4_out, and_5_out, and_6_out, and_7_out, bool_ruch_zapis,
       comparator_2_eq, comparator_2_lt, comparator_7_gt, comparator_8_lt, dot, info, nand_1_out, nand_2_out,
       nand_3_out, nand_4_out, not_1_out, or_1_out, or_4_out, pionek_ruch, pionek_start, player_blue,
       player_green, player_red, player_yellow;
  wire [3:0] rzut_liczba;
  wire [6:0] adder_1_out, multiplexer_1_out, transistor_1_out;

  random_generaor_main main_1 (.Cyfra(rzut_liczba), .out_2(info), .Kropka(dot), .Losuj(sygnal_losowania));
  Comparator #(.width(2), .mode("unsigned")) comparator_1 (
    .a(pion_info_odczyt[8:7]), .b(IN_ruch_ktorym_pionem), .eq(pionek_start));  // open: gt, lt
  not not_1 (not_1_out, pionek_start);
  Transistor #(.width(7)) transistor_1 (.in(pion_info_odczyt[6:0]), .out(transistor_1_out), .gate(not_1_out));
  Comparator #(.width(7)) comparator_2 (
    .a(transistor_1_out), .b(7'b0001111), .gt(pionek_ruch), .eq(comparator_2_eq), .lt(comparator_2_lt));
  Comparator #(.width(2), .mode("unsigned")) comparator_3 (
    .a(pion_info_odczyt[10:9]), .b(2'b00), .eq(player_red));  // open: gt, lt
  Comparator #(.width(2), .mode("unsigned")) comparator_4 (
    .a(pion_info_odczyt[10:9]), .b(2'b01), .eq(player_blue));  // open: gt, lt
  Comparator #(.width(2), .mode("unsigned")) comparator_5 (
    .a(pion_info_odczyt[10:9]), .b(2'b10), .eq(player_green));  // open: gt, lt
  Comparator #(.width(2), .mode("unsigned")) comparator_6 (
    .a(pion_info_odczyt[10:9]), .b(2'b11), .eq(player_yellow));  // open: gt, lt
  Register #(.width(7)) register_1 (.D({3'b000, rzut_liczba}), .Q(out_5), .clk(info));  // open: en, clr
  or or_1 (or_1_out, comparator_2_eq, comparator_2_lt);
  nand nand_1 (nand_1_out, dot, or_1_out, player_red);
  nand nand_2 (nand_2_out, dot, or_1_out, player_blue);
  nand nand_3 (nand_3_out, dot, or_1_out, player_green);
  nand nand_4 (nand_4_out, dot, or_1_out, player_yellow);
  and and_1 (and_1_out, pionek_start, dot, info);
  and and_2 (and_2_out, info, bool_ruch_zapis, pionek_ruch);
  Transistor #(.width(7)) transistor_2 (.in(7'b0010000), .out(Pion_Dane_do_zapisu[6:0]), .gate(nand_1_out));
  Transistor #(.width(7)) transistor_3 (.in(7'b0011010), .out(Pion_Dane_do_zapisu[6:0]), .gate(nand_2_out));
  Transistor #(.width(7)) transistor_4 (.in(7'b0100100), .out(Pion_Dane_do_zapisu[6:0]), .gate(nand_3_out));
  or or_2 (zapisz_dane, and_1_out, and_2_out);
  Transistor #(.width(7)) transistor_5 (.in(7'b0101110), .out(Pion_Dane_do_zapisu[6:0]), .gate(nand_4_out));
  and and_3 (and_3_out, info, pionek_ruch, player_red);
  and and_4 (and_4_out, info, pionek_ruch, player_blue);
  and and_5 (and_5_out, info, pionek_ruch, player_green);
  and and_6 (and_6_out, info, pionek_ruch, player_yellow);
  or or_3 (bool_ruch_zapis, and_3_out, or_4_out);
  Comparator #(.width(7), .mode("unsigned")) comparator_7 (
    .a(adder_1_out), .b(7'b0111000), .gt(comparator_7_gt));  // open: eq, lt
  Comparator #(.width(7), .mode("unsigned")) comparator_8 (
    .a(adder_1_out), .b(7'b0111011), .lt(comparator_8_lt));  // open: gt, eq
  or or_4 (or_4_out, and_4_out, and_5_out, and_6_out);
  Adder #(.width(7)) adder_1 (
    .a({3'b000, rzut_liczba}), .b(pion_info_odczyt[6:0]), .out(adder_1_out));  // open: cin, cout
  Multiplexer #(.width(7), .enable("false")) multiplexer_1 (
    .in0({7{1'b0}}), .in1(7'b0100111), .out(multiplexer_1_out), .sel(and_7_out));
  and and_7 (and_7_out, comparator_7_gt, comparator_8_lt, or_4_out);
  Subtractor #(.width(7)) subtractor_1 (
    .a(adder_1_out), .b(multiplexer_1_out), .out(Pion_Dane_do_zapisu[6:0]));  // open: bin, bout

  assign Pion_Dane_do_zapisu[10:7] = pion_info_odczyt[10:7];

  // Other names for the same wires on the sheet: stan_pion[6:0] = Pion_Dane_do_zapisu[6:0];
  //   nr_pionka[1:0] = pion_info_odczyt[8:7]; kolor[1:0] = pion_info_odczyt[10:9];
  //   Pozycja[6:0] = pion_info_odczyt[6:0]

  // Notes on the sheet:
  //   konwerter na 7 bitow
  //   Czerwony
  //   Niebieskiego
  //   Zielony
  //   Zółty
  //   Warunek czy pion jest na polu startowym
  //   #1 Wyjscie z bazy
  //   Warunki logiczne
  //   Force'owanie przerzucenia na pole start
  //   #2 poruszanie się po planszy
  //   sterowanie logiczne
  //   sterowanie na planszy/HANDLE przegięcie (B,G,Y)
  //   DORZUCIC WARUNEK ZE ODEJMIE JEZELI NIE JEST W BAZIE!!!!!!!!!
  //   #3 Handle exceptions
  //   #4 wejście do bazy
  //   #5 WIN
endmodule
