// Logisim project PlayerToBit.circ as structural Verilog: 1 circuit, main circuit main
module main (
  input  pion_1,
  input  pion_2,
  input  pion_3,
  input  pion_4,
  output [1:0] out_5
);

  wire and_1_out, not_1_out, not_2_out, not_3_out, not_4_out;

  not not_1 (not_1_out, pion_4);
  not not_2 (not_2_out, pion_3);
  and and_1 (and_1_out, not_1_out, not_2_out, not_4_out, not_3_out);
  assign out_5 = pion_1 ? 2'b00 : 2'bz;  // Controlled_Buffer controlled_buffer_1
  assign out_5 = pion_2 ? 2'b01 : 2'bz;  // Controlled_Buffer controlled_buffer_2
  assign out_5 = pion_3 ? 2'b10 : 2'bz;  // Controlled_Buffer controlled_buffer_3
  assign out_5 = pion_4 ? 2'b11 : 2'bz;  // Controlled_Buffer controlled_buffer_4
  not not_3 (not_3_out, pion_1);
  not not_4 (not_4_out, pion_2);
  assign out_5 = and_1_out ? 2'b00 : 2'bz;  // Controlled_Buffer controlled_buffer_5

  // Other names for the same wires on the sheet: s[1:0] = out_5
endmodule
