// Logisim project Rysowanie_pionka.circ as structural Verilog: 1 circuit, main circuit main
module main (
  input  [16:0] Kolor_X_Y,
  input  [1:0] jaki_gracz,
  input  CLK,
  output [6:0] wyjscie_y,
  output [6:0] wyjscie_x,
  output [15:0] wyjscie_rgb
);

  wire and_1_out, and_2_out, and_3_out, comparator_1_eq, comparator_2_eq, comparator_3_lt, comparator_4_eq,
       comparator_5_eq, comparator_6_eq, comparator_7_gt, comparator_8_eq, comparator_9_eq, comparator_10_eq,
       comparator_11_eq, comparator_12_eq, or_1_out, or_2_out, or_3_out, or_4_out, or_5_out;
  wire [6:0] counter_1_q, counter_2_q;
  wire [15:0] multiplexer_1_out, multiplexer_3_out;

  Comparator #(.width(7), .mode("unsigned")) comparator_1 (
    .a(counter_1_q), .b(7'b0000010), .eq(comparator_1_eq));  // open: gt, lt
  Comparator #(.width(7), .mode("unsigned")) comparator_2 (
    .a(counter_1_q), .b(7'b0000011), .eq(comparator_2_eq));  // open: gt, lt
  Comparator #(.width(7), .mode("unsigned")) comparator_3 (
    .a(counter_2_q), .b(7'b0000110), .lt(comparator_3_lt));  // open: gt, eq
  Comparator #(.width(7), .mode("unsigned")) comparator_4 (
    .a(counter_1_q), .b(7'b0000001), .eq(comparator_4_eq));  // open: gt, lt
  Comparator #(.width(7), .mode("unsigned")) comparator_5 (
    .a(counter_1_q), .b(7'b0000100), .eq(comparator_5_eq));  // open: gt, lt
  Comparator #(.width(7), .mode("unsigned")) comparator_6 (
    .a(counter_2_q), .b(7'b0000001), .eq(comparator_6_eq));  // open: gt, lt
  Comparator #(.width(7), .mode("unsigned")) comparator_7 (
    .a(counter_2_q), .b(7'b0000011), .gt(comparator_7_gt));  // open: eq, lt
  Comparator #(.width(7), .mode("unsigned")) comparator_8 (
    .a(counter_1_q), .b({7{1'b0}}), .eq(comparator_8_eq));  // open: gt, lt
  Comparator #(.width(7), .mode("unsigned")) comparator_9 (
    .a(counter_1_q), .b(7'b0000101), .eq(comparator_9_eq));  // open: gt, lt
  Comparator #(.width(7), .mode("unsigned")) comparator_10 (
    .a(counter_2_q), .b(7'b0000101), .eq(comparator_10_eq));  // open: gt, lt
  or or_1 (or_1_out, comparator_1_eq, comparator_2_eq);
  or or_2 (or_2_out, comparator_4_eq, comparator_5_eq);
  or or_3 (or_3_out, comparator_6_eq, comparator_7_gt);
  or or_4 (or_4_out, comparator_8_eq, comparator_9_eq);
  and and_1 (and_1_out, comparator_3_lt, or_1_out);
  and and_2 (and_2_out, or_2_out, or_3_out);
  and and_3 (and_3_out, or_4_out, comparator_10_eq);
  or or_5 (or_5_out, and_1_out, and_2_out, and_3_out);
  Multiplexer #(.select(2), .width(16), .enable("false")) multiplexer_1 (
    .in0(16'h3c00), .in1(16'hf), .in2(16'h1e0), .in3(16'h7e47), .out(multiplexer_1_out), .sel(jaki_gracz));
  Multiplexer #(.width(16), .enable("false")) multiplexer_2 (
    .in0(multiplexer_3_out), .in1(multiplexer_1_out), .out(wyjscie_rgb), .sel(or_5_out));
  Counter #(.width(7), .max('h7f)) counter_1 (
    .Q(counter_1_q), .clk(comparator_12_eq), .clr(comparator_11_eq));  // open: load, D, count, carry
  Counter #(.width(7), .max('h7f)) counter_2 (
    .Q(counter_2_q), .clk(CLK), .clr(comparator_12_eq));  // open: load, D, count, carry
  Multiplexer #(.select(3), .width(16), .enable("false")) multiplexer_3 (
    .in0(16'h7c00), .in1(16'h1f), .in2(16'h3e0), .in3(16'h7fe0), .in4({16{1'b1}}), .out(multiplexer_3_out),
    .sel(Kolor_X_Y[2:0]));  // open: in5, in6, in7
  Adder #(.width(7)) adder_1 (.a(Kolor_X_Y[9:3]), .b(counter_1_q), .out(wyjscie_x));  // open: cin, cout
  Comparator #(.width(7), .mode("unsigned")) comparator_11 (
    .a(counter_1_q), .b(7'b0000110), .eq(comparator_11_eq));  // open: gt, lt
  Adder #(.width(7)) adder_2 (.a(Kolor_X_Y[16:10]), .b(counter_2_q), .out(wyjscie_y));  // open: cin, cout
  Comparator #(.width(7), .mode("unsigned")) comparator_12 (
    .a(counter_2_q), .b(7'b0000110), .eq(comparator_12_eq));  // open: gt, lt

  // Notes on the sheet:
  //   Q kolumny
  //   Q wiersza
  //   niebieski
  //   zielony
  //   czerwony
  //   zolty
  //   Kolor pionka
  //   czerwony
  //   niebieski
  //   zielony
  //   zolty
  //   bialy
  //   kolumny
  //   wiersze
endmodule
