// Logisim project Rysowanie_pola.circ as structural Verilog: 1 circuit, main circuit main
module main (
  input  [16:0] Color_X_Y,
  input  CLK,
  output [6:0] Wyjscie_adres,
  output [6:0] Wyjscie_x,
  output [6:0] wyjscie_y,
  output [15:0] out_6
);

  wire comparator_1_eq, comparator_2_eq, comparator_3_eq;
  wire [6:0] counter_1_q, counter_2_q;

  Counter #(.width(7), .max('h7f)) counter_1 (
    .Q(counter_1_q), .clk(comparator_2_eq), .clr(comparator_1_eq));  // open: load, D, count, carry
  Counter #(.width(7), .max('h7f)) counter_2 (
    .Q(counter_2_q), .clk(CLK), .clr(comparator_2_eq));  // open: load, D, count, carry
  Comparator #(.width(7), .mode("unsigned")) comparator_1 (
    .a(counter_1_q), .b(7'b0000110), .eq(comparator_1_eq));  // open: gt, lt
  Comparator #(.width(7), .mode("unsigned")) comparator_2 (
    .a(counter_2_q), .b(7'b0000110), .eq(comparator_2_eq));  // open: gt, lt
  Counter #(.width(7), .max('h7f)) counter_3 (
    .Q(Wyjscie_adres), .clk(comparator_1_eq), .clr(comparator_3_eq));  // open: load, D, count, carry
  Adder #(.width(7)) adder_1 (.a(counter_1_q), .b(Color_X_Y[9:3]), .out(Wyjscie_x));  // open: cin, cout
  Adder #(.width(7)) adder_2 (.a(Color_X_Y[16:10]), .b(counter_2_q), .out(wyjscie_y));  // open: cin, cout
  Comparator #(.width(7)) comparator_3 (.a(Wyjscie_adres), .b(7'b1001000), .eq(comparator_3_eq));  // open: gt, lt
  Multiplexer #(.select(3), .width(16), .enable("false")) multiplexer_1 (
    .in0(16'h7c00), .in1(16'h1f), .in2(16'h3e0), .in3(16'h7fe0), .in4({16{1'b1}}), .out(out_6),
    .sel(Color_X_Y[2:0]));  // open: in5, in6, in7

  // Notes on the sheet:
  //   czerwony
  //   zielony
  //   zolty
  //   bialy
  //   Wyjscie kolor
endmodule
