// Logisim project aktualny_stan_planszy_RAM.circ as structural Verilog: 1 circuit, main circuit main
module main (
  input  CLK,
  input  [6:0] in_x,
  input  [6:0] in_y,
  input  [2:0] in_mux_rgb,
  output [6:0] Wyjscie_X,
  output [6:0] Wyjscie_Y,
  output [15:0] out_7
);

  wire comparator_1_eq, comparator_2_eq, comparator_3_eq, not_1_out, not_2_out, not_3_out;
  wire [2:0] ram_3_data;
  wire [6:0] counter_1_q, counter_2_q, counter_3_q, ram_1_data, ram_2_data;

  Counter #(.width(7), .max('h7f)) counter_1 (
    .Q(counter_1_q), .clk(comparator_2_eq), .clr(comparator_1_eq));  // open: load, D, count, carry
  Comparator #(.width(7)) comparator_1 (.a(counter_1_q), .b(7'b1001000), .eq(comparator_1_eq));  // open: gt, lt
  not not_1 (not_1_out, 1'b1);
  not not_2 (not_2_out, 1'b1);
  RAM #(.addrWidth(7), .dataWidth(7), .bus("separate")) ram_1 (
    .addr(counter_1_q), .din(in_x), .data(ram_1_data), .str(1'b1), .sel(1'b1), .clk(CLK), .ld(not_1_out));  // open: clr
  RAM #(.addrWidth(7), .dataWidth(7), .bus("separate")) ram_2 (
    .addr(counter_1_q), .din(in_y), .data(ram_2_data), .str(1'b1), .sel(1'b1), .clk(CLK), .ld(not_2_out));  // open: clr
  RAM #(.addrWidth(7), .dataWidth(3), .bus("separate")) ram_3 (
    .addr(counter_1_q), .din(in_mux_rgb), .data(ram_3_data), .str(1'b1), .sel(1'b1), .clk(CLK), .ld(not_3_out));  // open: clr
  not not_3 (not_3_out, 1'b1);
  Counter #(.width(7), .max('h7f)) counter_2 (
    .Q(counter_2_q), .clk(comparator_3_eq), .clr(comparator_2_eq));  // open: load, D, count, carry
  Adder #(.width(7)) adder_1 (.b(counter_2_q), .out(Wyjscie_X));  // open: a, cin, cout
  Comparator #(.width(7), .mode("unsigned")) comparator_2 (
    .a(counter_2_q), .b(7'b0000110), .eq(comparator_2_eq));  // open: gt, lt
  Adder #(.width(7)) adder_2 (.a(ram_2_data), .b(counter_3_q), .out(Wyjscie_Y));  // open: cin, cout
  Counter #(.width(7), .max('h7f)) counter_3 (
    .Q(counter_3_q), .clk(CLK), .clr(comparator_3_eq));  // open: load, D, count, carry
  Comparator #(.width(7), .mode("unsigned")) comparator_3 (
    .a(counter_3_q), .b(7'b0000110), .eq(comparator_3_eq));  // open: gt, lt
  Multiplexer #(.select(3), .width(16), .enable("false")) multiplexer_1 (
    .in0(16'h7c00), .in1(16'h1f), .in2(16'h3e0), .in3(16'h7fe0), .in4({16{1'b1}}), .out(out_7),
    .sel(ram_3_data));  // open: in5, in6, in7

  // Notes on the sheet:
  //   KOLOR
  //   X
  //   Y
  //   kolumny
  //   wiersze
  //   czerwony
  //   niebieski
  //   zielony
  //   zolty
  //   bialy
  //   Wyjscie kolor
endmodule
