// Logisim project chinczyk_game.circ as structural Verilog: 1 circuit, main circuit main
module main (
  input  [1:0] nr_pionka,
  input  zakoncz_ture,
  input  losuj,
  input  mozesz_ruszyc,
  output [1:0] mux_kolor_outside,
  output [4:0] liczba,
  output mozesz_losowac,
  output out_8,
  output [6:0] Y,
  output [6:0] X,
  output [15:0] RGB
);

  wire and_1_out, and_2_out, and_3_out, clock_1_out, clock_2_out, clock_3_out, clock_4_out, comparator_1_eq,
       counter_2_q, main_2_clk_save, main_2_zapiszz, multiplexer_2_out, multiplexer_4_out, multiplexer_6_out,
       multiplexer_7_out, not_1_out, not_2_out, not_5_out, not_6_out, not_7_out, siema, undriven,
       zablokuj_petle;
  wire [1:0] ram_2_data_2, ram_2_data_3;
  wire [3:0] counter_3_q, main_1_siema, multiplexer_3_out;
  wire [6:0] main_1_out_2, main_3_wyjscie_adres, main_3_wyjscie_x, main_3_wyjscie_y, main_4_wyjscie_x,
       main_4_wyjscie_y, multiplexer_1_out, ram_2_data;
  wire [11:0] main_1_wyjscie_stan_pionka, main_2_pion_dane_do_zapisu, multiplexer_5_out, register_1_q;
  wire [11:11] ram_2_data_4;
  wire [15:0] main_3_out_6, main_4_wyjscie_rgb;
  wire [16:0] main_1_out_3, ram_1_data;

  Counter #(.width(2), .max('h3)) counter_1 (
    .Q(mux_kolor_outside), .clk(zakoncz_ture));  // open: load, D, count, carry, clr
  not not_1 (not_1_out, counter_2_q);
  Clock clock_1 (.out(clock_1_out));
  and and_1 (and_1_out, not_1_out, clock_1_out);
  Register #(.width(12), .trigger("falling")) register_1 (
    .D({ram_2_data_4[11], ram_2_data_3, ram_2_data_2, ram_2_data}), .Q(register_1_q), .clk(and_3_out));  // open: en, clr
  inicjalizacja_main main_1 (
    .CLK(and_1_out), .out_2(main_1_out_2), .Wyjscie_Stan_pionka(main_1_wyjscie_stan_pionka),
    .siema(main_1_siema), .out_3(main_1_out_3));
  LOGIKAGRY__1____kopia_main main_2 (
    .pion_info_odczyt(register_1_q), .IN_ruch_ktorym_pionem(nr_pionka),
    .Pion_Dane_do_zapisu(main_2_pion_dane_do_zapisu), .IN_ktory_gracz(mux_kolor_outside),
    .CLK_SAVE(main_2_clk_save), .out_10(liczba[4]), .ZAPISZZ(main_2_zapiszz), .out_9(liczba[3:0]),
    .sygnal_losowania(losuj), .akceptuj_ruch(mozesz_ruszyc), .zakoncz_ture(zakoncz_ture), .out_13(out_8));  // open: podglad
  not not_2 (not_2_out, losuj);
  Comparator #(.width(7)) comparator_1 (.a(main_1_out_2), .b(7'b1001000), .eq(comparator_1_eq));  // open: gt, lt
  not not_3 (mozesz_losowac, siema);
  Counter #(.width(1), .max('h1)) counter_2 (
    .Q(counter_2_q), .clk(comparator_1_eq));  // open: load, D, count, carry, clr
  Clock clock_2 (.out(clock_2_out));
  Multiplexer #(.width(7), .enable("false")) multiplexer_1 (
    .in0(main_1_out_2), .in1(main_3_wyjscie_adres), .out(multiplexer_1_out), .sel(counter_2_q));
  Clock clock_3 (.out(clock_3_out));
  Multiplexer #(.enable("false")) multiplexer_2 (
    .in0(clock_3_out), .in1(undriven), .out(multiplexer_2_out), .sel(counter_2_q));
  Multiplexer #(.width(4), .enable("false")) multiplexer_3 (
    .in0(main_1_siema), .in1(counter_3_q), .out(multiplexer_3_out), .sel(counter_2_q));
  not not_4 (zablokuj_petle, main_2_zapiszz);
  and and_2 (and_2_out, counter_2_q, not_2_out, clock_2_out);
  Multiplexer #(.enable("false")) multiplexer_4 (.in0(1'b1), .in1(1'b0), .out(multiplexer_4_out), .sel(counter_2_q));
  Counter #(.width(4), .max('hf)) counter_3 (.Q(counter_3_q), .clk(and_3_out));  // open: load, D, count, carry, clr
  and and_3 (and_3_out, clock_4_out, zablokuj_petle, not_5_out);
  not not_5 (not_5_out, siema);
  Clock clock_4 (.out(clock_4_out));
  Hex_Digit_Display hex_digit_display_1 (.value(liczba[3:0]), .dp(liczba[4]));
  Multiplexer #(.width(12), .enable("false")) multiplexer_5 (
    .in0(main_1_wyjscie_stan_pionka), .in1(main_2_pion_dane_do_zapisu), .out(multiplexer_5_out),
    .sel(counter_2_q));
  Multiplexer #(.enable("false")) multiplexer_6 (
    .in0(multiplexer_2_out), .in1(main_2_clk_save), .out(multiplexer_6_out), .sel(counter_2_q));
  Multiplexer #(.enable("false")) multiplexer_7 (
    .in0(multiplexer_4_out), .in1(main_2_zapiszz), .out(multiplexer_7_out), .sel(counter_2_q));
  RAM #(.addrWidth(7), .dataWidth(17), .bus("separate")) ram_1 (
    .addr(multiplexer_1_out), .din(main_1_out_3), .data(ram_1_data), .str(multiplexer_4_out), .sel(1'b1),
    .clk(multiplexer_2_out), .ld(not_6_out));  // open: clr
  not not_6 (not_6_out, multiplexer_4_out);
  RAM #(.addrWidth(4), .dataWidth(12), .bus("separate")) ram_2 (
    .addr(multiplexer_3_out), .din(multiplexer_5_out),
    .data({ram_2_data_4[11], ram_2_data_3, ram_2_data_2, ram_2_data}), .str(multiplexer_7_out), .sel(1'b1),
    .clk(multiplexer_6_out), .ld(not_7_out));  // open: clr
  not not_7 (not_7_out, multiplexer_7_out);
  Comparator #(.width(7)) comparator_2 (.a(multiplexer_1_out), .b(ram_2_data), .eq(siema));  // open: gt, lt
  Rysowanie_pola_main main_3 (
    .CLK(and_2_out), .Wyjscie_x(main_3_wyjscie_x), .wyjscie_y(main_3_wyjscie_y), .out_6(main_3_out_6),
    .Wyjscie_adres(main_3_wyjscie_adres), .Color_X_Y(ram_1_data));
  Rysowanie_pionka_main main_4 (
    .wyjscie_x(main_4_wyjscie_x), .jaki_gracz(ram_2_data_3), .CLK(and_2_out),
    .wyjscie_rgb(main_4_wyjscie_rgb), .wyjscie_y(main_4_wyjscie_y), .Kolor_X_Y(ram_1_data));
  Multiplexer #(.width(7), .enable("false")) multiplexer_8 (
    .in0(main_3_wyjscie_x), .in1(main_4_wyjscie_x), .out(X), .sel(siema));
  Multiplexer #(.width(7), .enable("false")) multiplexer_9 (
    .in0(main_3_wyjscie_y), .in1(main_4_wyjscie_y), .out(Y), .sel(siema));
  Multiplexer #(.width(16), .enable("false")) multiplexer_10 (
    .in0(main_3_out_6), .in1(main_4_wyjscie_rgb), .out(RGB), .sel(siema));

  // Notes on the sheet:
  //   dane
  //   Na 0 nie losuj bo "tracisz" rzut
  //   zmiana sterowania
  //   Pion_info
  //   Zapis?
  //   Zalecana najwyższa częstotliwość
  //   Stan planszy kolor X Y
  //   Bool Czy jest tam pion?
endmodule
