// Logisim project inicjalizacja.circ as structural Verilog: 1 circuit, main circuit main
module main (
  input  CLK,
  output [6:0] out_2,
  output [16:0] out_3,
  output [11:0] Wyjscie_Stan_pionka,
  output [3:0] siema
);

  wire comparator_1_eq, comparator_2_eq, comparator_3_eq;
  wire [6:0] adder_1_out, adder_2_out, counter_3_q, counter_4_q;
  wire [10:0] rom_4_data;

  Counter #(.width(7), .max('h7f)) counter_1 (
    .Q(out_2), .clk(comparator_2_eq), .clr(comparator_1_eq));  // open: load, D, count, carry
  Comparator #(.width(7)) comparator_1 (.a(out_2), .b(7'b1001000), .eq(comparator_1_eq));  // open: gt, lt
  Counter #(.width(4), .max('hf)) counter_2 (.Q(siema), .clk(comparator_2_eq));  // open: load, D, count, carry, clr
  ROM #(.addrWidth(7), .dataWidth(7)) rom_1 (.addr(out_2), .data(out_3[9:3]));  // open: sel
  ROM #(.addrWidth(7), .dataWidth(7)) rom_2 (.addr(out_2), .data(out_3[16:10]));  // open: sel
  ROM #(.addrWidth(7), .dataWidth(3)) rom_3 (.addr(out_2), .data(out_3[2:0]));  // open: sel
  ROM #(.addrWidth(4), .dataWidth(11)) rom_4 (.addr(siema), .data(rom_4_data));  // open: sel
  assign Wyjscie_Stan_pionka = {{1{1'b0}}, rom_4_data};  // Bit_Extender bit_extender_1
  Counter #(.width(7), .max('h7f)) counter_3 (
    .Q(counter_3_q), .clk(comparator_3_eq), .clr(comparator_2_eq));  // open: load, D, count, carry
  Counter #(.width(7), .max('h7f)) counter_4 (
    .Q(counter_4_q), .clk(CLK), .clr(comparator_3_eq));  // open: load, D, count, carry
  Adder #(.width(7)) adder_1 (.a(out_3[9:3]), .b(counter_3_q), .out(adder_1_out));  // open: cin, cout
  Comparator #(.width(7), .mode("unsigned")) comparator_2 (
    .a(counter_3_q), .b(7'b0000110), .eq(comparator_2_eq));  // open: gt, lt
  Adder #(.width(7)) adder_2 (.a(out_3[16:10]), .b(counter_4_q), .out(adder_2_out));  // open: cin, cout
  Comparator #(.width(7), .mode("unsigned")) comparator_3 (
    .a(counter_4_q), .b(7'b0000110), .eq(comparator_3_eq));  // open: gt, lt
  Multiplexer #(.select(3), .width(16), .enable("false")) multiplexer_1 (
    .in0(16'h7c00), .in1(16'h1f), .in2(16'h3e0), .in3(16'h7fe0), .in4({16{1'b1}}), .sel(out_3[2:0]));  // open: in5, in6, in7, out

  // Notes on the sheet:
  //   ADRES X
  //   ADRESY
  //   KOLOR
  //   contents of rom_1 (hex, n*v repeats v):
  //   15 1d 15 1d 5d 65 5d 65 5d 65 5d 65 15 1d 15 1d 15 1d 25 2d 5*35 3d 5*45 4d 55 5d 65 65 65 5d 55 4d
  //   5*45 3d 5*35 2d 25 1d 15 15 1d 25 2d 35 4*3d 45 4d 55 5d 4*3d
  //   contents of rom_2 (hex, n*v repeats v):
  //   15 15 1d 1d 15 15 1d 1d 5d 5d 65 65 5d 5d 65 65 5*35 2d 25 1d 15 15 15 1d 25 2d 5*35 3d 5*45 4d 55
  //   5d 65 65 65 5d 55 4d 5*45 5*3d 1d 25 2d 35 4*3d 45 4d 55 5d
  //   contents of rom_3 (hex, n*v repeats v):
  //   4*0 4*1 4*2 4*3 0 9*4 1 9*4 2 9*4 3 9*4 4*0 4*1 4*2 4*3
  //   contents of rom_4 (hex, n*v repeats v):
  //   0 81 102 183 204 285 306 387 408 489 50a 58b 60c 68d 70e 78f
  //   kolumny
  //   wiersze
  //   czerwony
  //   niebieski
  //   zielony
  //   zolty
  //   bialy
endmodule
