// Logisim project random_generaor.circ as structural Verilog: 1 circuit, main circuit main
module main (
  input  Losuj,
  output out_2,
  output [3:0] Cyfra,
  output Kropka
);

  wire clock_1_out, comparator_2_eq, comparator_3_eq, comparator_4_eq, nor_1_out, not_1_out, or_1_out,
       or_2_out;
  wire [1:0] counter_1_q;
  wire [2:0] random_1_out;

  Clock clock_1 (.out(clock_1_out));
  nor nor_1 (nor_1_out, out_2, clock_1_out);
  or or_1 (or_1_out, not_1_out, or_2_out);
  not not_1 (not_1_out, Losuj);
  Counter #(.width(2), .max('h3)) counter_1 (
    .Q(counter_1_q), .clk(nor_1_out), .clr(or_1_out));  // open: load, D, count, carry
  Comparator #(.width(2)) comparator_1 (.a(counter_1_q), .b(2'b11), .eq(out_2));  // open: gt, lt
  Random #(.width(3)) random_1 (.clk(nor_1_out), .next(Losuj), .out(random_1_out));  // open: clr
  Comparator #(.width(3), .mode("unsigned")) comparator_2 (
    .a(random_1_out), .b(3'b111), .eq(comparator_2_eq));  // open: gt, lt
  Comparator #(.width(3), .mode("unsigned")) comparator_3 (
    .a(random_1_out), .b(3'b000), .eq(comparator_3_eq));  // open: gt, lt
  Comparator #(.width(3), .mode("unsigned")) comparator_4 (
    .a(random_1_out), .b(3'b110), .eq(comparator_4_eq));  // open: gt, lt
  // NOT_Gate not_2 has open pins: in=out_2, out=open
  // Transmission_Gate #(.width(4)) transmission_1: pin names not known; wires that end beside it: {1'b0, random_1_out}, out_2, Cyfra
  or or_2 (or_2_out, comparator_2_eq, comparator_3_eq);
  and and_1 (Kropka, out_2, comparator_4_eq, Losuj);

  // Notes on the sheet:
  //   Info o wylosowaniu
endmodule
