// Logisim project rzuty.circ as structural Verilog: 1 circuit, main circuit main
module main (
  input  zakoncz_ture,
  input  kulnij,
  input  info,
  input  dot,
  output out_5
);

  wire and_1_out, counter_1_q, multiplexer_1_out, not_1_out;

  Counter #(.width(1), .max('h1)) counter_1 (
    .Q(counter_1_q), .clk(and_1_out), .clr(zakoncz_ture));  // open: load, D, count, carry
  and and_1 (and_1_out, kulnij, info, not_1_out);
  not not_1 (not_1_out, dot);
  Multiplexer #(.enable("false")) multiplexer_1 (.in0(1'b0), .in1(1'b1), .out(multiplexer_1_out), .sel(counter_1_q));
  Subtractor #(.width(1)) subtractor_1 (.a(1'b1), .b(multiplexer_1_out), .out(out_5));  // open: bin, bout

  // Notes on the sheet:
  //   Zalozenia:
  //   Kulniecie zmniejsza liczbe o 1
endmodule
